# Fritzing sketch Cell Balancing (saved by Fritzing 0.9.3b)
breadboards: 1

parts:
  Part2 = Arduino Mega 2560 (Rev3)
  BAT10 = Battery Holders [package=battery-aaa]
  BAT11 = Battery Holders [package=battery-aaa]
  BAT12 = Battery Holders [package=battery-aaa]
  BAT13 = Battery Holders [package=battery-aaa]
  BAT14 = Battery Holders [package=battery-aaa]
  BAT15 = Battery Holders [package=battery-aaa]
  BAT16 = Battery Holders [package=battery-aaa]
  BAT17 = Battery Holders [package=battery-aaa]
  BAT18 = Battery Holders [package=battery-aaa]
  Q5 = Basic FET N-Channel [package="DPak [SMD]"]
  Q6 = Basic FET N-Channel [package="DPak [SMD]"]
  Q7 = Basic FET N-Channel [package="DPak [SMD]"]
  Q8 = Basic FET N-Channel [package="DPak [SMD]"]
  D9 = Rectifier Diode 10A [part_number=P1000K]
  D10 = Rectifier Diode 10A [part_number=P1000K]
  D11 = Rectifier Diode 10A [part_number=P1000K]
  D12 = Rectifier Diode 10A [part_number=P1000K]
  L2 = Inductor [package="0603 [SMD]"]
  D13 = Rectifier Diode 10A [part_number=P1000K]
  D14 = Rectifier Diode 10A [part_number=P1000K]
  D15 = Rectifier Diode 10A [part_number=P1000K]
  D16 = Rectifier Diode 10A [part_number=P1000K]
  Q9 = Basic FET N-Channel [package="DPak [SMD]"]
  Q10 = Basic FET N-Channel [package="DPak [SMD]"]
  Q11 = Basic FET N-Channel [package="DPak [SMD]"]
  Q12 = Basic FET N-Channel [package="DPak [SMD]"]

nets:
  N1: Part2.D13_PWM, Q8.Gate
  N2: Part2.GND, BAT10.-, BAT11.-, BAT12.-
  N3: Part2.D4_PWM, Q7.Gate
  N4: Part2.D31, Q6.Gate
  N5: Part2.D32, Q5.Gate
  N6: Part2.D33, Q12.Gate
  N7: Part2.D34, Q11.Gate
  N8: Part2.D35, Q10.Gate
  N9: Part2.D36, Q9.Gate
  N10: BAT10.+, BAT11.+, BAT12.+, BAT13.-, BAT14.-, BAT15.-
  N11: BAT13.+, BAT14.+, BAT15.+, BAT16.-, BAT17.-, BAT18.-
  N12: BAT16.+, BAT17.+, BAT18.+, Q5.drain, D9.cathode
  N13: Q5.source, D13.anode
  N14: Q6.drain, D10.cathode
  N15: Q6.source, D14.anode
  N16: Q7.drain, D11.cathode
  N17: Q7.source, D15.anode
  N18: Q8.drain, D12.cathode
  N19: Q8.source, D16.anode
  N20: D9.anode, Q9.source
  N21: D10.anode, Q10.source
  N22: D11.anode, Q11.source
  N23: D12.anode, Q12.source
  N24: L2.pin_0, D13.cathode, D14.cathode, D15.cathode, D16.cathode
  N25: L2.pin_1, Q9.drain, Q10.drain, Q11.drain, Q12.drain
