# Fritzing sketch Current sensor (saved by Fritzing 0.9.3b)
breadboards: 1

parts:
  Part1 = Arduino Mega 2560 (Rev3)
  BAT10 = Battery Holders [package=battery-aaa]
  BAT11 = Battery Holders [package=battery-aaa]
  BAT12 = Battery Holders [package=battery-aaa]
  BAT13 = Battery Holders [package=battery-aaa]
  BAT14 = Battery Holders [package=battery-aaa]
  BAT15 = Battery Holders [package=battery-aaa]
  BAT16 = Battery Holders [package=battery-aaa]
  BAT17 = Battery Holders [package=battery-aaa]
  BAT18 = Battery Holders [package=battery-aaa]
  Part11 = ACS712 Low Current Sensor Board v12
  Part12 = ACS712 Low Current Sensor Board v12
  Part13 = ACS712 Low Current Sensor Board v12
  Part14 = ACS712 Low Current Sensor Board v12
  Part15 = ACS712 Low Current Sensor Board v12
  Part16 = ACS712 Low Current Sensor Board v12
  Part17 = ACS712 Low Current Sensor Board v12
  Part18 = ACS712 Low Current Sensor Board v12
  Part19 = ACS712 Low Current Sensor Board v12
  U4 = 74HC4067 [package=ssop24]

nets:
  N1: Part1.A8, U4.COM
  5V: Part1.IOREF, Part11.5V, Part12.5V, Part13.5V, Part14.5V, Part15.5V, Part16.5V, Part17.5V, Part18.5V, Part19.5V, U4.VCC
  GND: Part1.GND, BAT10.-, BAT11.-, BAT12.-, Part11.GND, Part12.GND, Part13.GND, Part14.GND, Part15.GND, Part16.GND, Part17.GND, Part18.GND, Part19.GND, U4.GND
  N2: Part1.D25, U4.S0
  N3: Part1.D26, U4.S1
  N4: Part1.D27, U4.S2
  N5: Part1.D28, U4.S3
  N6: BAT10.+, Part13.IP+, Part14.IP-
  N7: BAT11.+, Part11.IP-, Part14.IP+
  N8: BAT12.+, BAT13.-, BAT14.-, BAT15.-, Part11.IP+, Part13.IP-
  N9: BAT13.+, Part15.IP+, Part16.IP-
  N10: BAT14.+, BAT16.-, BAT17.-, BAT18.-, Part12.IP+, Part15.IP-
  N11: BAT15.+, Part12.IP-, Part16.IP+
  N12: BAT16.+, Part17.IP-, Part19.IP+
  N13: BAT17.+, Part18.IP+, Part19.IP-
  N14: BAT18.+, Part17.IP+, Part18.IP-
  N15: Part11.VO, U4.CHAN7
  N16: Part12.VO, U4.CHAN4
  N17: Part13.VO, U4.CHAN6
  N18: Part14.VO, U4.CHAN8
  N19: Part15.VO, U4.CHAN3
  N20: Part16.VO, U4.CHAN5
  N21: Part17.VO, U4.CHAN2
  N22: Part18.VO, U4.CHAN1
  N23: Part19.VO, U4.CHAN0
