# Fritzing sketch MOSFET Connection (saved by Fritzing 0.9.3b)
breadboards: 1

parts:
  Part1 = Arduino Mega 2560 (Rev3)
  Q1 = Basic FET N-Channel [package="DPak [SMD]"]
  Q2 = Basic FET N-Channel [package="DPak [SMD]"]
  Q3 = Basic FET N-Channel [package="DPak [SMD]"]
  Q4 = Basic FET N-Channel [package="DPak [SMD]"]
  Q5 = Basic FET N-Channel [package="DPak [SMD]"]
  Q6 = Basic FET N-Channel [package="DPak [SMD]"]
  Q7 = Basic FET N-Channel [package="DPak [SMD]"]
  Q8 = Basic FET N-Channel [package="DPak [SMD]"]
  D1 = Diode [package=diode-1n4148]
  D2 = Diode [package=diode-1n4148]
  D3 = Diode [package=diode-1n4148]
  D4 = Diode [package=diode-1n4148]
  D5 = Diode [package=diode-1n4148]
  D6 = Diode [package=diode-1n4148]
  D7 = Diode [package=diode-1n4148]
  D8 = Diode [package=diode-1n4148]
  L1 = Inductor [package="0805 [SMD]"]

nets:
  N1: Part1.D13_PWM, Q6.Gate
  N2: Part1.D4_PWM, Q5.Gate
  N3: Part1.D31, Q4.Gate
  N4: Part1.D32, Q2.Gate
  N5: Part1.D33, Q3.Gate
  N6: Part1.D34, Q1.Gate
  N7: Part1.D35, Q8.Gate
  N8: Part1.D38, Q7.Gate
  N9: Q1.drain, Q2.drain, Q3.drain, L1.pin_0
  N10: Q1.source, D3.A
  N11: Q2.source, D8.A
  N12: Q3.source, D6.A
  N13: Q4.source, D7.A
  N14: Q5.drain, D3.C
  N15: Q5.source, D5.A
  N16: Q6.drain, D6.C
  N17: Q6.source, D1.A
  N18: Q7.drain, D8.C
  N19: Q7.source, D4.A
  N20: Q8.drain, D7.C
  N21: Q8.source, D2.A
  N22: D1.C, D2.C, D4.C, D5.C, L1.pin_1
