# Fritzing sketch Temperature sensor (saved by Fritzing 0.9.3b)
breadboards: 1

parts:
  Part1 = Arduino Mega 2560 (Rev3)
  BAT10 = Battery Holders [package=battery-aaa]
  BAT11 = Battery Holders [package=battery-aaa]
  BAT12 = Battery Holders [package=battery-aaa]
  BAT13 = Battery Holders [package=battery-aaa]
  BAT14 = Battery Holders [package=battery-aaa]
  BAT15 = Battery Holders [package=battery-aaa]
  BAT16 = Battery Holders [package=battery-aaa]
  BAT17 = Battery Holders [package=battery-aaa]
  BAT18 = Battery Holders [package=battery-aaa]
  U4 = 74HC4067 [package=ssop24]
  T10 = LM35 Temperature Sensor [package="TO92 [THT]"]
  T11 = LM35 Temperature Sensor [package="TO92 [THT]"]
  T12 = LM35 Temperature Sensor [package="TO92 [THT]"]
  T13 = LM35 Temperature Sensor [package="TO92 [THT]"]
  T14 = LM35 Temperature Sensor [package="TO92 [THT]"]
  T15 = LM35 Temperature Sensor [package="TO92 [THT]"]
  T16 = LM35 Temperature Sensor [package="TO92 [THT]"]
  T17 = LM35 Temperature Sensor [package="TO92 [THT]"]
  T18 = LM35 Temperature Sensor [package="TO92 [THT]"]

nets:
  N1: Part1.A9, U4.COM
  5V: Part1.5V, U4.VCC
  GND: Part1.GND, U4.GND, T10.GND, T11.GND, T12.GND
  N2: Part1.D25, U4.S0
  N3: Part1.D26, U4.S1
  N4: Part1.D27, U4.S2
  N5: Part1.D28, U4.S3
  N6: BAT10.-, BAT11.-, BAT12.-
  N7: BAT10.+, BAT11.+, BAT12.+, BAT13.-, BAT14.-, BAT15.-, T10.+Vs, T11.+Vs, T12.+Vs
  N8: BAT13.+, BAT14.+, BAT15.+, BAT16.-, BAT17.-, BAT18.-, T13.+Vs, T14.+Vs, T15.+Vs
  N9: BAT16.+, BAT17.+, BAT18.+, T16.+Vs, T17.+Vs, T18.+Vs
  N10: U4.CHAN7, T11.Vout
  N11: U4.CHAN6, T12.Vout
  N12: U4.CHAN5, T13.Vout
  N13: U4.CHAN4, T14.Vout
  N14: U4.CHAN3, T15.Vout
  N15: U4.CHAN2, T16.Vout
  N16: U4.CHAN1, T17.Vout
  N17: U4.CHAN0, T18.Vout
  N18: U4.CHAN8, T10.Vout
  GND_2: T13.GND, T14.GND, T15.GND
  GND_3: T16.GND, T17.GND, T18.GND
